// Logisim project FUSION.circ as structural Verilog: 1 circuit, main circuit main
module main (
  input  [15:0] Instruction,
  output [31:0] S,
  output [1:0] Flags
);

  // RM rm_1: pin names not known; wires that end beside it: S, Flags
endmodule
